# Fritzing sketch Thermostat (saved by Fritzing 0.9.3b)
breadboards: 1

parts:
  U1 = NodeMCU V3.0
  RHT1 = Humidity and Temperature Sensor RHT03
  Part1 = songle relay
  D1 = Rectifier Diode [part_number=1N4001 package="300 mil [THT]"]
  Q1 = NPN-Transistor [package="TO92 [THT]"]
  R1 = Resistor [tolerance=±5% resistance=1k package=THT]
  OLED_I2C1 = OLED 128x64 I2C Monochrome Display

nets:
  N1: U1.D1, OLED_I2C1.SCK
  N2: U1.D2, OLED_I2C1.SDA
  N3: U1.D4, RHT1.Data-signal
  N4: U1.GND#6, U1.GND#13, U1.GND#16, U1.GND#33
  N5: U1.D5, R1.Pin_1
  VCC: RHT1.Vcc, Part1.VCC, D1.cathode, OLED_I2C1.VDD
  N6: RHT1.GND_1, Q1.C, OLED_I2C1.GND
  N7: D1.anode, Q1.E
  N8: Q1.B, R1.Pin_0

notes:
  The resistor should be a 680 ohm on a 3.3 v setup

custom parts:
  NodeMCU V3.0: ESP8266 based NodeMCU
